# Fritzing sketch Bluetooth_with_motor (saved by Fritzing 0.9.3b)

parts:
  Part1 = Arduino Uno (Rev3)
  Part3 = Bluetooth HC-05 Macho
  DJI_ESC_30A2 = DJI 30A ESC
  920KV_Motor2 = DJI 920 KV Motor
  920KV_Motor3 = DJI 920 KV Motor
  920KV_Motor4 = DJI 920 KV Motor
  920KV_Motor5 = DJI 920 KV Motor
  DJI_ESC_30A3 = DJI 30A ESC
  DJI_ESC_30A4 = DJI 30A ESC
  DJI_ESC_30A5 = DJI 30A ESC
  Power_plug2 = Power plug

nets:
  N1: Part1.D8, DJI_ESC_30A2.DATA
  N2: Part1.D9_PWM, DJI_ESC_30A4.DATA
  N3: Part1.D10_PWM/SS, DJI_ESC_30A3.DATA
  N4: Part1.D11_PWM/MOSI, DJI_ESC_30A5.DATA
  GND: Part1.GND, Part3.GND, DJI_ESC_30A3.GND
  N5: Part1.D0/RX, Part3.TXD
  N6: Part1.D1/TX, Part3.RXD
  5V: Part1.5V, Part3.VCC
  N7: DJI_ESC_30A2.U, 920KV_Motor2.v
  N8: DJI_ESC_30A2.V, 920KV_Motor2.u
  N9: DJI_ESC_30A2.W, 920KV_Motor2.w
  N10: 920KV_Motor3.w, DJI_ESC_30A4.W
  N11: 920KV_Motor3.v, DJI_ESC_30A4.U
  N12: 920KV_Motor3.u, DJI_ESC_30A4.V
  N13: 920KV_Motor4.w, DJI_ESC_30A3.W
  N14: 920KV_Motor4.v, DJI_ESC_30A3.U
  N15: 920KV_Motor4.u, DJI_ESC_30A3.V
  N16: 920KV_Motor5.w, DJI_ESC_30A5.W
  N17: 920KV_Motor5.v, DJI_ESC_30A5.U
  N18: 920KV_Motor5.u, DJI_ESC_30A5.V
  N19: DJI_ESC_30A4.GROUND, Power_plug2.GND
  +12V: DJI_ESC_30A4.+12V, Power_plug2.VCC

custom parts:
  DJI 920 KV Motor: DJI Brushless Outrunner 2212/920K Motor F330-550
